# Fritzing sketch scout-weatherstation (saved by Fritzing 0.9.3b)

parts:
  Part1 = Arduino Pro Mini (3.3V)
  Grove1 = Grove OLED 128x96
  Part2 = Digital Temperature Sensor Breakout - TMP102
  VCC1 = 4 x AAA Battery Mount

nets:
  N1: Part1.A4, Grove1.SDA, Part2.GND
  N2: Part1.A5, Grove1.SCL, Part2.SCL
  N3: Part1.RAW, VCC1.+
  GND: Part1.GND, Grove1.GND, Part2.SDA, VCC1.-
  VCC: Part1.VCC, Grove1.VCC, Part2.V+
